// Digital circuit 08_09_2023_MOD.dig as structural Verilog
module _08_09_2023_MOD (
  input  CLK,
  input  DDIN,
  input  in_4,
  output [7:0] DO
);

  wire and_1_out, and_2_out, and_3_out, and_4_out, AOX, enADD, enSUB, multiplexer_11_out, nor_1_out,
       nor_2_out, not_1_out, or_1_out, SELADRR, SSLD, SWTADDR, tALUFLG, tCAR, tDDDS, tFETCH, tPC_plus, tWRYN,
       tZER, WRTMEM, Z1, Z2, Z3, Z4;
  wire [1:0] tCHDS, tCHDSo, tDISTDEC, tSRC;
  wire [2:0] MPC_out, RGCAR_q;
  wire [3:0] tOPER;
  wire [7:0] ANDOP, BIOS_d, DALU, DDxx, DIMEM, iR0, iR1, iR2, iR3, MSUMM_s, multiplexer_5_out,
       multiplexer_6_out, OROP, RAMM_d, undriven, xor_1_out, XOROP;
  wire [7:4] FETCH_q;
  wire [9:3] RMADR_d;
  wire [15:0] PC_out, SRCMEM, tADDR;

  RAMDualPort #(.AddrBits(16), .Bits(8)) RAMM (.A(tADDR), .Din(DIMEM), .str(WRTMEM), .C(CLK), .ld(1'b1), .D(RAMM_d));
  ROM #(.AddrBits(11), .Bits(8)) BIOS (.A(tADDR[10:0]), .sel(1'b1), .D(BIOS_d));
  Counter #(.Bits(16)) PC (.en(tPC_plus), .C(CLK), .clr(1'b0), .out(PC_out));  // open: ovf
  Multiplexer #(.Bits(16)) multiplexer_1 (.sel(SELADRR), .in_0(PC_out), .in_1(SRCMEM), .out(tADDR));
  nor nor_1 (nor_1_out, tADDR[11], tADDR[12], tADDR[13], tADDR[14], tADDR[15]);
  or or_1 (or_1_out, enSUB, AOX);
  Multiplexer #(.Bits(8)) multiplexer_2 (.sel(nor_1_out), .in_0(RAMM_d), .in_1(BIOS_d), .out(DO));
  Counter #(.Bits(3)) MPC (.en(1'b1), .C(CLK), .clr(tFETCH), .out(MPC_out));  // open: ovf
  LookUpTable u_SSLD (.in0(tDDDS), .in1(SELADRR), .in2(WRTMEM), .in3(or_1_out), .out(SSLD));
  Multiplexer #(.Bits(8)) multiplexer_3 (.sel(SSLD), .in_0(DIMEM), .in_1(DO), .out(DDxx));
  Register #(.Bits(8)) FETCH (.D(DO), .C(CLK), .en(tFETCH), .Q({FETCH_q, tSRC, tDISTDEC}));
  ROM #(.AddrBits(8), .Bits(7)) RMADR (.A({FETCH_q, tSRC, tDISTDEC}), .sel(1'b1), .D(RMADR_d));
  ROM #(.AddrBits(10), .Bits(11)) MICRPRG (
    .A({RMADR_d, MPC_out}), .sel(1'b1), .D({SWTADDR, WRTMEM, SELADRR, tDDDS, tOPER, tPC_plus, tFETCH, tWRYN}));
  and and_1 (and_1_out, tOPER[3], tDDDS);
  and and_2 (and_2_out, tOPER[2], tDDDS);
  and and_3 (and_3_out, tOPER[1], tDDDS);
  and and_4 (and_4_out, tOPER[0], tDDDS);
  and and_5 (enADD, ~tOPER[2], ~tOPER[1], ~tOPER[3], tOPER[0]);  // And
  and and_6 (enSUB, tOPER[0], ~tOPER[1], tOPER[2], ~tOPER[3]);  // And
  LookUpTable ANDORXORRev (.in0(and_1_out), .in1(and_2_out), .in2(and_3_out), .in3(and_4_out), .out(AOX));
  Multiplexer #(.Bits(2)) multiplexer_4 (.sel(nor_2_out), .in_0(tDISTDEC), .in_1(tCHDS), .out(tCHDSo));
  nor nor_2 (nor_2_out, enADD, AOX, enSUB);
  Multiplexer #(.Selector_Bits(2), .Bits(8)) multiplexer_5 (
    .sel(tCHDSo), .in_0(iR0), .in_1(iR1), .in_2(iR2), .in_3(iR3), .out(multiplexer_5_out));
  Multiplexer #(.Bits(8)) multiplexer_6 (.sel(tDDDS), .in_0(DO), .in_1(multiplexer_5_out), .out(multiplexer_6_out));
  assign xor_1_out = multiplexer_6_out ^ {8{enSUB}};  // XOr xor_1, 8 bits wide
  Add #(.Bits(8)) MSUMM (.a(DDxx), .b(xor_1_out), .c_i(tALUFLG), .s(MSUMM_s), .c_o(tCAR));
  assign ANDOP = DDxx & multiplexer_6_out;  // And and_7, 8 bits wide
  assign OROP = DDxx | multiplexer_6_out;  // Or or_2, 8 bits wide
  assign XOROP = DDxx ^ multiplexer_6_out;  // XOr xor_2, 8 bits wide
  Multiplexer #(.Bits(16)) multiplexer_7 (.sel(SWTADDR), .in_0({iR1, iR0}), .in_1({iR3, iR2}), .out(SRCMEM));
  regFile regfile_1 (.DI(DALU), .clk(CLK), .DST(tDISTDEC), .WREN(tWRYN), .R0(iR0), .R1(iR1), .R2(iR2), .R3(iR3));
  // Probe on tOPER
  Multiplexer #(.Selector_Bits(4), .Bits(8)) multiplexer_8 (
    .sel(tOPER), .in_0(multiplexer_6_out), .in_1(MSUMM_s), .in_2(ANDOP), .in_3(OROP), .in_4(XOROP),
    .in_5(MSUMM_s), .in_6(multiplexer_6_out), .in_7(8'h1), .in_8(8'h1), .in_9(8'h1), .in_10(8'h1),
    .in_11(8'h1), .in_12(8'h1), .in_13(8'h1), .in_14(8'h1), .in_15(8'h1), .out(DALU));
  Multiplexer #(.Selector_Bits(2), .Bits(8)) multiplexer_9 (
    .sel(tCHDS), .in_0(iR0), .in_1(iR1), .in_2(iR2), .in_3(iR3), .out(DIMEM));
  not not_1 (not_1_out, CLK);
  // Probe on iR0
  Multiplexer #(.Bits(2)) multiplexer_10 (.sel(tDDDS), .in_0(tDISTDEC), .in_1(tSRC), .out(tCHDS));
  Register #(.Bits(3)) RGCAR (
    .D({DALU[7], tCAR, tZER}), .C(multiplexer_11_out), .en(1'b1), .Q({RGCAR_q[2], tALUFLG, RGCAR_q[0]}));
  nor nor_3 (tZER, DALU[0], DALU[1], DALU[2], DALU[3], DALU[4], DALU[5], DALU[6], DALU[7]);
  // Probe on iR1
  // Probe on iR2
  Multiplexer multiplexer_11 (.sel(enSUB), .in_0(CLK), .in_1(not_1_out), .out(multiplexer_11_out));
  // Probe on iR3
  DigPIL digpil_1 (
    .SEG(undriven), ._4(Z1), ._3(Z2), ._2(Z3), ._1(Z4), ._11(iR0), ._22(iR1), ._33(iR2), ._44(iR3), .S(in_4),
    .DINN(DDIN));
  Seven_Seg #(.commonCathode("true"), .persistTime(10)) seven_seg_1 (
    .a(undriven[3]), .b(undriven[2]), .c(undriven[1]), .d(undriven[0]), .e(undriven[4]), .f(undriven[5]),
    .g(undriven[6]), .dp(undriven[7]), .common(Z1));
  Seven_Seg #(.commonCathode("true"), .persistTime(10)) seven_seg_2 (
    .a(undriven[3]), .b(undriven[2]), .c(undriven[1]), .d(undriven[0]), .e(undriven[4]), .f(undriven[5]),
    .g(undriven[6]), .dp(undriven[7]), .common(Z2));
  Seven_Seg #(.commonCathode("true"), .persistTime(10)) seven_seg_3 (
    .a(undriven[3]), .b(undriven[2]), .c(undriven[1]), .d(undriven[0]), .e(undriven[4]), .f(undriven[5]),
    .g(undriven[6]), .dp(undriven[7]), .common(Z3));
  Seven_Seg #(.commonCathode("true"), .persistTime(10)) seven_seg_4 (
    .a(undriven[3]), .b(undriven[2]), .c(undriven[1]), .d(undriven[0]), .e(undriven[4]), .f(undriven[5]),
    .g(undriven[6]), .dp(undriven[7]), .common(Z4));

  // Other names for the same wires on the sheet: tSIG = DALU[7]; SetRG = in_4; tCLK = CLK; tDO[7:0] = DO

  // Notes on the sheet:
  //   DDIN: Hz: 500
  //   MUX ADDRR
  //   contents of BIOS (hex, n*v repeats v):
  //   e0,1,e1,8,e2,a,38,e2,5,e3,3,b2,b3,0,e2,2,e3,8,e0,a,33,e0,5,e1
  //   ,3,b8,b9
  //   Switch DO reg to mem SUB oper.
  //   PROJECT OF SIMPLE PROCESSOR 2023
  //   contents of SSLD (hex, n*v repeats v):
  //   11*0,1
  //   contents of RMADR (hex, n*v repeats v):
  //   16*0,4*7,4*8,4*9,4*a,0,0,1f,20,4*27,21,22,0,0,4*28,0,0,0,23,0,0,0
  //   ,24,25,0,0,0,26,0,0,0,4*b,4*c,4*d,4*e,0,0,29,29,4*0,2a,2a,6*0
  //   ,4*13,4*14,4*15,4*16,0,0,2e,2e,4*0,2d,2d,6*0,4*17,4*18,4*19,4*1a
  //   ,0,0,2f,2f,4*0,30,30,6*0,4*1b,4*1c,4*1d,4*1e,0,0,31,31,4*0,32,32
  //   ,6*0,4*f,4*10,4*11,4*12,0,0,12b,2b,4*0,2c,2c,6*0,4*1,8*0,4*2,4*3
  //   ,4*4,4*5,4*6
  //   contents of MICRPRG (hex, n*v repeats v):
  //   6,7*0,5,6,6*0,d,e,6*0,15,16,6*0,1d,6,6*0,25,26,6*0,2d,2e,6*0,87
  //   ,7*0,87,7*0,87,7*0,87,7*0,8f,7*0,8f,7*0,8f,7*0,8f,7*0,af,7*0,af
  //   ,7*0,af,7*0,af,7*0,97,7*0,97,7*0,97,7*0,97,7*0,9f,7*0,9f,7*0,9f
  //   ,7*0,9f,7*0,a7,7*0,a7,7*0,a7,7*0,a7,7*0,131,6,6*0,131,6,6*0,531
  //   ,6,6*0,531,6,6*0,7ba,7*0,7ba,7*0,3ba,7*0,3ba,7*0,48f,7*0,42f,7*0
  //   ,10b,6,6*0,50b,7*0,1ab,7*0,5ab,7*0,593,7*0,193,7*0,19b,7*0,59b
  //   ,7*0,1a3,7*0,5a3
  //   contents of ANDORXORRev (hex, n*v repeats v):
  //   0,0,1,1,1,7*0,1
  //   MUX DIST
  //   ADD one CONVERT to C2
  //   Carr FLAG
  //   MUX SOURCE
  //   Sw. R0R1 to R2R3
  //   FLAGS
  //   R1 (8-8 bit)
  //   R2 (8-8 bit)
  //   R0 (8-8) bit
  //   R3 (8-8 bit)
endmodule
