// Digital circuit CntIE10.dig as structural Verilog
module CntIE10 (
  input  CS,
  input  CLK,
  output _1,
  output _2,
  output _4,
  output _8,
  output CRY
);

  wire d_ff_as_1_nq, d_ff_as_2_nq, d_ff_as_3_nq, d_ff_as_4_nq, or_1_out;

  or or_1 (or_1_out, CRY, CS);
  D_FF_AS d_ff_as_1 (.Set(1'b0), .D(d_ff_as_1_nq), .C(CLK), .Clr(or_1_out), .Q(_1), .nQ(d_ff_as_1_nq));
  and and_1 (CRY, _8, ~_4, _2, ~_1);  // And
  D_FF_AS d_ff_as_2 (.Set(1'b0), .D(d_ff_as_2_nq), .C(d_ff_as_1_nq), .Clr(or_1_out), .Q(_2), .nQ(d_ff_as_2_nq));
  D_FF_AS d_ff_as_3 (.Set(1'b0), .D(d_ff_as_3_nq), .C(d_ff_as_2_nq), .Clr(or_1_out), .Q(_4), .nQ(d_ff_as_3_nq));
  D_FF_AS d_ff_as_4 (.Set(1'b0), .D(d_ff_as_4_nq), .C(d_ff_as_3_nq), .Clr(or_1_out), .Q(_8), .nQ(d_ff_as_4_nq));
endmodule
