// Digital circuit DigPIL.dig as structural Verilog
module DigPIL (
  input  [7:0] SEG,
  input  _4,
  input  _3,
  input  _2,
  input  _1,
  output DINN,
  output [7:0] _11,
  output [7:0] _22,
  output [7:0] _33,
  output [7:0] _44,
  output S
);

  wire _1din_q, decoder_1_out_0, decoder_1_out_1, decoder_1_out_2, decoder_1_out_3, multiplexer_3_out,
       multiplexer_4_out, multiplexer_5_out, multiplexer_6_out, not_1_out, not_2_out, R01A, R01B, R01C, R01D,
       R02A, R02B, R02C, R02D, R04A, R04B, R04C, R04D, R08A, R08B, R08C, R08D;
  wire [1:0] Comm;

  Multiplexer #(.Bits(8)) multiplexer_1 (
    .sel(S), .in_0(_11), .in_1(_33), .out({R08B, R04B, R02B, R01B, R08A, R04A, R02A, R01A}));
  Multiplexer #(.Bits(8)) multiplexer_2 (
    .sel(S), .in_0(_22), .in_1(_44), .out({R08D, R04D, R02D, R01D, R08C, R04C, R02C, R01C}));
  not not_1 (not_1_out, DINN);
  T_FF _1din (.T(not_1_out), .C(DINN), .Q(_1din_q), .nQ(Comm[0]));
  Multiplexer #(.Selector_Bits(2)) multiplexer_3 (
    .sel(Comm), .in_0(R01D), .in_1(R01C), .in_2(R01B), .in_3(R01A), .out(multiplexer_3_out));
  Multiplexer #(.Selector_Bits(2)) multiplexer_4 (
    .sel(Comm), .in_0(R02D), .in_1(R02C), .in_2(R02B), .in_3(R02A), .out(multiplexer_4_out));
  Multiplexer #(.Selector_Bits(2)) multiplexer_5 (
    .sel(Comm), .in_0(R04D), .in_1(R04C), .in_2(R04B), .in_3(R04A), .out(multiplexer_5_out));
  Multiplexer #(.Selector_Bits(2)) multiplexer_6 (
    .sel(Comm), .in_0(R08D), .in_1(R08C), .in_2(R08B), .in_3(R08A), .out(multiplexer_6_out));
  not not_2 (not_2_out, _1din_q);
  T_FF _2din (.T(not_2_out), .C(_1din_q), .nQ(Comm[1]));  // open: Q
  LookUpTable #(.Bits(8)) K514ID2 (
    .in0(multiplexer_3_out), .in1(multiplexer_4_out), .in2(multiplexer_5_out), .in3(multiplexer_6_out),
    .out(SEG));
  Decoder #(.Selector_Bits(2)) decoder_1 (
    .sel(Comm), .out_0(decoder_1_out_0), .out_1(decoder_1_out_1), .out_2(decoder_1_out_2),
    .out_3(decoder_1_out_3));
  not not_3 (_4, decoder_1_out_0);
  not not_4 (_3, decoder_1_out_1);
  not not_5 (_2, decoder_1_out_2);
  not not_6 (_1, decoder_1_out_3);

  // Notes on the sheet:
  //   Dynamic indication PIL
  //   1
  //   2
  //   4
  //   8
  //   contents of K514ID2 (hex, n*v repeats v):
  //   3f,6,5d,4f,66,6b,7b,e,7f,6f,7e,73,39,57,79,78
endmodule
