// Digital circuit Dinamic_dig.dig as structural Verilog
module Dinamic_dig (
  input  DIN,
  input  SINHRO
);

  wire _1a, _1b, _1c, _1d, _1din_q, _2a, _2b, _2c, _2d, _3a, _3b, _3c, _3d, _4a, _4b, _4c, _4d,
       decoder_1_out_0, decoder_1_out_1, decoder_1_out_2, decoder_1_out_3, IE1_2_cry, IE1_3_cry, IE1_4_cry,
       multiplexer_1_out, multiplexer_2_out, multiplexer_3_out, multiplexer_4_out, not_1_out, not_2_out,
       not_3_out, not_4_out, not_5_out, not_6_out, pullup_1_out;
  wire [1:0] Comm;
  wire [7:0] K514ID2_out;

  PullUp pullup_1 (.out(pullup_1_out));
  CntIE10 IE1 (._1(_4a), ._2(_4b), ._4(_4c), ._8(_4d), .CLK(IE1_2_cry), .CS(pullup_1_out));  // open: CRY
  CntIE10 IE1_2 (._1(_3a), ._2(_3b), ._4(_3c), ._8(_3d), .CRY(IE1_2_cry), .CLK(IE1_3_cry), .CS(pullup_1_out));
  CntIE10 IE1_3 (._1(_2a), ._2(_2b), ._4(_2c), ._8(_2d), .CRY(IE1_3_cry), .CLK(IE1_4_cry), .CS(pullup_1_out));
  CntIE10 IE1_4 (._1(_1a), ._2(_1b), ._4(_1c), ._8(_1d), .CRY(IE1_4_cry), .CLK(SINHRO), .CS(pullup_1_out));
  Switch switch_1 (.A(pullup_1_out), .B(1'b0));
  Multiplexer #(.Selector_Bits(2)) multiplexer_1 (
    .sel(Comm), .in_0(_4a), .in_1(_3a), .in_2(_2a), .in_3(_1a), .out(multiplexer_1_out));
  Multiplexer #(.Selector_Bits(2)) multiplexer_2 (
    .sel(Comm), .in_0(_4b), .in_1(_3b), .in_2(_2b), .in_3(_1b), .out(multiplexer_2_out));
  Multiplexer #(.Selector_Bits(2)) multiplexer_3 (
    .sel(Comm), .in_0(_4c), .in_1(_3c), .in_2(_2c), .in_3(_1c), .out(multiplexer_3_out));
  Multiplexer #(.Selector_Bits(2)) multiplexer_4 (
    .sel(Comm), .in_0(_4d), .in_1(_3d), .in_2(_2d), .in_3(_1d), .out(multiplexer_4_out));
  not not_1 (not_1_out, DIN);
  T_FF _1din (.T(not_1_out), .C(DIN), .Q(_1din_q), .nQ(Comm[0]));
  not not_2 (not_2_out, _1din_q);
  T_FF _2din (.T(not_2_out), .C(_1din_q), .nQ(Comm[1]));  // open: Q
  LookUpTable #(.Bits(8)) K514ID2 (
    .in0(multiplexer_1_out), .in1(multiplexer_2_out), .in2(multiplexer_3_out), .in3(multiplexer_4_out),
    .out(K514ID2_out));
  Decoder #(.Selector_Bits(2)) decoder_1 (
    .sel(Comm), .out_0(decoder_1_out_0), .out_1(decoder_1_out_1), .out_2(decoder_1_out_2),
    .out_3(decoder_1_out_3));
  Seven_Seg #(.commonCathode("true"), .persistTime(10)) seven_seg_1 (
    .a(K514ID2_out[3]), .b(K514ID2_out[2]), .c(K514ID2_out[1]), .d(K514ID2_out[0]), .e(K514ID2_out[4]),
    .f(K514ID2_out[5]), .g(K514ID2_out[6]), .dp(K514ID2_out[7]), .common(not_3_out));
  Seven_Seg #(.commonCathode("true"), .persistTime(10)) seven_seg_2 (
    .a(K514ID2_out[3]), .b(K514ID2_out[2]), .c(K514ID2_out[1]), .d(K514ID2_out[0]), .e(K514ID2_out[4]),
    .f(K514ID2_out[5]), .g(K514ID2_out[6]), .dp(K514ID2_out[7]), .common(not_4_out));
  not not_3 (not_3_out, decoder_1_out_0);
  not not_4 (not_4_out, decoder_1_out_1);
  Seven_Seg #(.commonCathode("true"), .persistTime(10)) seven_seg_3 (
    .a(K514ID2_out[3]), .b(K514ID2_out[2]), .c(K514ID2_out[1]), .d(K514ID2_out[0]), .e(K514ID2_out[4]),
    .f(K514ID2_out[5]), .g(K514ID2_out[6]), .dp(K514ID2_out[7]), .common(not_5_out));
  Seven_Seg #(.commonCathode("true"), .persistTime(10)) seven_seg_4 (
    .a(K514ID2_out[3]), .b(K514ID2_out[2]), .c(K514ID2_out[1]), .d(K514ID2_out[0]), .e(K514ID2_out[4]),
    .f(K514ID2_out[5]), .g(K514ID2_out[6]), .dp(K514ID2_out[7]), .common(not_6_out));
  not not_5 (not_5_out, decoder_1_out_2);
  not not_6 (not_6_out, decoder_1_out_3);

  // Notes on the sheet:
  //   DIN: Hz: 200
  //   SINHRO: Hz: 2
  //   Dynamic indication 2023
  //   1
  //   2
  //   4
  //   8
  //   contents of K514ID2 (hex, n*v repeats v):
  //   3f,6,5d,4f,66,6b,7b,e,7f,6f,7e,73,39,57,79,78
endmodule
