// Digital circuit prcALU.dig as structural Verilog
module prcALU (
  input  clk,
  input  [2:0] tOPER,
  input  [7:0] R0,
  input  [7:0] R1,
  input  [7:0] R2,
  input  [7:0] R3,
  input  [7:0] tDO,
  input  [1:0] tDISTDEC,
  input  [1:0] tSRC,
  input  tDDDS,
  output carrOUT,
  output [7:0] DL
);

  wire add_1_c_o, or_1_out, tCAR;
  wire [1:0] multiplexer_5_out;
  wire [7:0] add_1_s, ANDOP, multiplexer_1_out, multiplexer_2_out, multiplexer_4_out, OROP, xor_2_out, XOROP;
  wire [7:7] and_1_out;

  or or_1 (or_1_out, tOPER[2], tOPER[1], tOPER[0]);
  and and_1 (and_1_out[7], tOPER[2], ~tOPER[1], tOPER[0]);  // And
  xor xor_1 (carrOUT, tCAR, and_1_out[7]);
  Multiplexer #(.Selector_Bits(2), .Bits(8)) multiplexer_1 (
    .sel(tDISTDEC), .in_0(R0), .in_1(R1), .in_2(R2), .in_3(R3), .out(multiplexer_1_out));
  assign xor_2_out = multiplexer_2_out ^ {8{and_1_out[7]}};  // XOr xor_2, 8 bits wide
  Multiplexer #(.Bits(8)) multiplexer_2 (.sel(or_1_out), .in_0(tDO), .in_1(multiplexer_1_out), .out(multiplexer_2_out));
  Add #(.Bits(8)) add_1 (.a(multiplexer_4_out), .b(xor_2_out), .c_i(tCAR), .s(add_1_s), .c_o(add_1_c_o));
  assign ANDOP = multiplexer_4_out & multiplexer_2_out;  // And and_2, 8 bits wide
  assign OROP = multiplexer_4_out | multiplexer_2_out;  // Or or_2, 8 bits wide
  assign XOROP = multiplexer_4_out ^ multiplexer_2_out;  // XOr xor_3, 8 bits wide
  Multiplexer #(.Selector_Bits(3), .Bits(8)) multiplexer_3 (
    .sel(tOPER), .in_0(multiplexer_2_out), .in_1(add_1_s), .in_2(ANDOP), .in_3(OROP), .in_4(XOROP),
    .in_5(add_1_s), .in_6(multiplexer_4_out), .in_7(8'h1), .out(DL));
  Register register_1 (.D(add_1_c_o), .C(clk), .en(1'b1), .Q(tCAR));
  Multiplexer #(.Selector_Bits(2), .Bits(8)) multiplexer_4 (
    .sel(multiplexer_5_out), .in_0(R0), .in_1(R1), .in_2(R2), .in_3(R3), .out(multiplexer_4_out));
  Multiplexer #(.Bits(2)) multiplexer_5 (.sel(tDDDS), .in_0(tDISTDEC), .in_1(tSRC), .out(multiplexer_5_out));

  // Other names for the same wires on the sheet: R00[7:0] = R0; R01[7:0] = R1; R02[7:0] = R2; R03[7:0] = R3;
  //   tCLK = clk; tDISTC[1:0] = tDISTDEC

  // Notes on the sheet:
  //   MODULE OF ALU
endmodule
