// Digital circuit regFile.dig as structural Verilog
module regFile (
  input  [7:0] DI,
  input  clk,
  input  [1:0] DST,
  input  WREN,
  output [7:0] R0,
  output [7:0] R1,
  output [7:0] R2,
  output [7:0] R3
);

  wire and_1_out, and_2_out, and_3_out, and_4_out, decoder_1_out_0, decoder_1_out_1, decoder_1_out_2,
       decoder_1_out_3;

  Decoder #(.Selector_Bits(2)) decoder_1 (
    .sel(DST), .out_0(decoder_1_out_0), .out_1(decoder_1_out_1), .out_2(decoder_1_out_2),
    .out_3(decoder_1_out_3));
  and and_1 (and_1_out, decoder_1_out_0, WREN);
  and and_2 (and_2_out, decoder_1_out_1, WREN);
  and and_3 (and_3_out, decoder_1_out_2, WREN);
  and and_4 (and_4_out, decoder_1_out_3, WREN);
  Register #(.Bits(8)) u_R0 (.D(DI), .C(clk), .en(and_1_out), .Q(R0));
  Register #(.Bits(8)) u_R1 (.D(DI), .C(clk), .en(and_2_out), .Q(R1));
  Register #(.Bits(8)) u_R2 (.D(DI), .C(clk), .en(and_3_out), .Q(R2));
  Register #(.Bits(8)) u_R3 (.D(DI), .C(clk), .en(and_4_out), .Q(R3));

  // Other names for the same wires on the sheet: tDREG[7:0] = DI

  // Notes on the sheet:
  //   REGISTERS
endmodule
